# Fritzing sketch Schematic_Fritizing (saved by Fritzing 0.9.5d)
breadboards: 1

parts:
  Arduino_Uno = Arduino Uno (Rev3) - ICSP
  KeyPad = 4x4 Keypad [part_number=101207]
  Red_Led = LED - 3mm [color="Red (633nm)" package="3 mm [THT]"]
  Green_Led = LED - 3mm [color="Green (570nm)" package="3 mm [THT]"]
  R1 = Resistor [tolerance=±5% resistance=220 package="2512 [SMD]"]
  R2 = Resistor [tolerance=±5% resistance=220 package="2512 [SMD]"]
  Servo_Motor = Basic Servo

nets:
  N1: Arduino_Uno.ICSP_MISO, Arduino_Uno.D12/MISO, Green_Led.anode
  5V: Arduino_Uno.5V, Servo_Motor.vcc
  N2: Arduino_Uno.ICSP_MOSI, Arduino_Uno.D11_PWM/MOSI, KeyPad.1
  N3: Arduino_Uno.GND, R2.Pin_0
  N4: Arduino_Uno.D8, KeyPad.4
  N5: Arduino_Uno.D9_PWM, KeyPad.3
  N6: Arduino_Uno.D10_PWM/SS, KeyPad.2
  N7: Arduino_Uno.D2, Red_Led.anode
  N8: Arduino_Uno.D3_PWM, Servo_Motor.pulse
  N9: Arduino_Uno.D4, KeyPad.8
  N10: Arduino_Uno.D5_PWM, KeyPad.7
  N11: Arduino_Uno.D6_PWM, KeyPad.6
  N12: Arduino_Uno.D7, KeyPad.5
  N13: Red_Led.cathode, R1.Pin_1, Servo_Motor.gnd
  N14: Green_Led.cathode, R1.Pin_0, R2.Pin_1

custom parts:
  4x4 Keypad: Matrix membrane keypad 4x4
