# Fritzing sketch Schematic_Fritizing (saved by Fritzing 0.9.5d)
breadboards: 1

parts:
  Seven_Digit_Display_Common_Anode = 7 Segment Display
  Arduino_Uno = Arduino Uno (Rev3) - ICSP
  R1 = Resistor [tolerance=±5% resistance=560 package="0805 [SMD]"]
  R2 = Resistor [tolerance=±5% resistance=560 package="0805 [SMD]"]
  R3 = Resistor [tolerance=±5% resistance=560 package="0805 [SMD]"]
  R4 = Resistor [tolerance=±5% resistance=560 package="0805 [SMD]"]
  R5 = Resistor [tolerance=±5% resistance=560 package="0805 [SMD]"]
  R6 = Resistor [tolerance=±5% resistance=560 package="0805 [SMD]"]
  R7 = Resistor [tolerance=±5% resistance=560 package="0805 [SMD]"]
  R8 = Resistor [tolerance=±5% resistance=560 package="0805 [SMD]"]
  Green_Button = Pushbutton [package="[THT]"]
  Red_Button = Pushbutton [package="[SMD]"]
  Relay_Module = KY-019 5V Relay Module [package="Breakout board"]
  LED1 = smd LED [color="Red (633nm)" package="1206 [SMD]"]
  R9 = Resistor [tolerance=±5% resistance=220 package="0805 [SMD]"]

nets:
  N1: Seven_Digit_Display_Common_Anode.Segment_E, R3.Pin_1
  N2: Seven_Digit_Display_Common_Anode.Segment_D, R2.Pin_1
  N3: Seven_Digit_Display_Common_Anode.common_anode, R8.Pin_1, Relay_Module.+, Relay_Module.Common
  N4: Seven_Digit_Display_Common_Anode.Segment_C, R5.Pin_1
  N5: Seven_Digit_Display_Common_Anode.Segment_B, R1.Pin_1
  N6: Seven_Digit_Display_Common_Anode.Segment_A, R4.Pin_1
  N7: Seven_Digit_Display_Common_Anode.Segment_F, R6.Pin_1
  N8: Seven_Digit_Display_Common_Anode.Segment_G, R7.Pin_1
  N9: Arduino_Uno.5V, R8.Pin_0
  N10: Arduino_Uno.D8, R3.Pin_0
  N11: Arduino_Uno.D9_PWM, R6.Pin_0
  N12: Arduino_Uno.D10_PWM/SS, R7.Pin_0
  N13: Arduino_Uno.D11_PWM/MOSI, Relay_Module.S
  N14: Arduino_Uno.GND, Green_Button.Pin_1, Green_Button.Pin_2, Red_Button.Pin_1, Red_Button.Pin_2, Relay_Module.-, R9.Pin_1
  N15: Arduino_Uno.D2, Red_Button.Pin_3, Red_Button.Pin_4
  N16: Arduino_Uno.D3_PWM, Green_Button.Pin_3, Green_Button.Pin_4
  N17: Arduino_Uno.D4, R4.Pin_0
  N18: Arduino_Uno.D5_PWM, R1.Pin_0
  N19: Arduino_Uno.D6_PWM, R5.Pin_0
  N20: Arduino_Uno.D7, R2.Pin_0
  N21: Relay_Module.NO, LED1.anode
  N22: LED1.cathode, R9.Pin_0

custom parts:
  KY-019 5V Relay Module: KY-019 5V Relay module, used to control AC circuits. (Special thanks to vanepp for fixing the PCB holes and other errors)
