# Fritzing sketch Schematic_Fritizing (saved by Fritzing 0.9.5d)
breadboards: 1

parts:
  Red_Led = LED - 5mm [color="Red (633nm)" package="5 mm [THT]"]
  Green_Led = LED - 5mm [color="Green (570nm)" package="5 mm [THT]"]
  Blue_Led = LED - 5mm [color="Blue (525nm)" package="5 mm [THT]"]
  LED4 = LED - 5mm [color="Yellow (595nm)" package="5 mm [THT]"]
  R1 = Resistor [tolerance=±5% resistance=220 package="0402 [SMD]"]
  R2 = Resistor [tolerance=±5% resistance=220 package="0402 [SMD]"]
  R3 = Resistor [tolerance=±5% resistance=220 package="0402 [SMD]"]
  R4 = Resistor [tolerance=±5% resistance=220 package="0402 [SMD]"]
  Arduino_Uno = Arduino Uno (Rev3)
  Red_Button = Pushbutton [package="[SMD]"]
  Green_Button = Pushbutton [package="[SMD]"]
  Blue_Button = Pushbutton [package="[SMD]"]
  Yellow_Button = Pushbutton [package="[SMD]"]

nets:
  N1: Red_Led.cathode, R1.Pin_1
  N2: Red_Led.anode, Arduino_Uno.D4
  N3: Green_Led.cathode, R3.Pin_1
  N4: Green_Led.anode, Arduino_Uno.D5_PWM
  N5: Blue_Led.cathode, R2.Pin_1
  N6: Blue_Led.anode, Arduino_Uno.D6_PWM
  N7: LED4.cathode, R4.Pin_1
  N8: LED4.anode, Arduino_Uno.D7
  N9: R1.Pin_0, R2.Pin_0, R3.Pin_0, R4.Pin_0, Arduino_Uno.GND, Red_Button.Pin_1, Red_Button.Pin_2, Green_Button.Pin_2, Blue_Button.Pin_1, Blue_Button.Pin_2, Yellow_Button.Pin_1, Yellow_Button.Pin_2
  N10: Arduino_Uno.D8, Red_Button.Pin_3, Red_Button.Pin_4
  N11: Arduino_Uno.D9_PWM, Green_Button.Pin_3
  N12: Arduino_Uno.D10_PWM/SS, Blue_Button.Pin_3
  N13: Arduino_Uno.D11_PWM/MOSI, Yellow_Button.Pin_3
